# Fritzing sketch schematic (saved by Fritzing 0.9.3b)

parts:
  Part1 = Arduino Uno (Rev3) - ICSP
  J3 = Infrared Proximity Sensor
  Part2 = OLED Monochrome 128x64 0.96 inch [part_number=326]

nets:
  N1: Part1.A0, J3.Vout
  GND: Part1.GND, J3.GND, Part2.GND
  N2: Part1.A4/SDA, Part2.MOSI_SDA
  N3: Part1.A5/SCL, Part2.SCLK_SCK
  N4: Part1.D4, Part2.RESET
  3V3: Part1.3V3, Part2.3.3V
  5V: Part1.5V, J3.Vcc

custom parts:
  OLED Monochrome 128x64 0.96 inch: These displays are small, only about 1" diameter, but very readable due to the high contrast of an OLED display. This display is made of 128x64 individual white OLED pixels, each one is turned on or off by the controller chip. Because the display makes its own light, no backlight is required. This reduces the power required to run the OLED and is why the display has such high contrast; we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
